// Logisim project Proyecto3.circ as structural Verilog: 1 circuit, main circuit main
module main (
  input  in_1
);

  wire button_1_out, Clk, multiplexer_1_out;
  wire [2:0] Seleccion;
  wire [7:0] counter_1_q, DIRSALTO;
  wire [11:3] rom_1_data;

  Button button_1 (.out(button_1_out));
  Multiplexer #(.select(3), .enable("false")) multiplexer_1 (
    .in0(1'b1), .in1(button_1_out), .in2(button_1_out), .in3(button_1_out), .in4(button_1_out),
    .in5(button_1_out), .in6(button_1_out), .in7(1'b0), .out(multiplexer_1_out), .sel(Seleccion));
  DotMatrix #(.matrixcols(3), .matrixrows(1)) dotmatrix_1 (
    .col0(Seleccion[2]), .col1(Seleccion[1]), .col2(Seleccion[0]));
  Clock clock_1 (.out(Clk));
  Counter #(.ongoal("continue")) counter_1 (
    .clr(in_1), .load(multiplexer_1_out), .up(1'b1), .count(1'b1), .clk(Clk), .D(DIRSALTO), .Q(counter_1_q));  // open: carry
  Hex_Digit_Display hex_digit_display_1 (.value(counter_1_q[7:4]));  // open: dp
  Hex_Digit_Display hex_digit_display_2 (.value(DIRSALTO[7:4]));  // open: dp
  Hex_Digit_Display hex_digit_display_3 (.value(counter_1_q[3:0]));  // open: dp
  ROM #(.dataWidth(20)) rom_1 (.addr(counter_1_q), .data({DIRSALTO, rom_1_data, Seleccion}));
  Hex_Digit_Display hex_digit_display_4 (.value(DIRSALTO[3:0]));  // open: dp
  DotMatrix #(.matrixcols(8), .matrixrows(1)) dotmatrix_2 (
    .col0(rom_1_data[11]), .col1(rom_1_data[10]), .col2(rom_1_data[9]), .col3(rom_1_data[8]),
    .col4(rom_1_data[7]), .col5(rom_1_data[6]), .col6(rom_1_data[5]), .col7(rom_1_data[4]));
  // also tied to GND on the sheet: rom_1_data[3]

  // Notes on the sheet:
  //   contents of rom_1 (hex, n*v repeats v):
  //   0 10 20 30 40 50 60 70 80 90 a0 b0 c0 d0 e0 f0 100 110 120 130 140 150 160 170 180 190 1a0 1b0 1c0
  //   1d0 1e0 1f0 200 210 220 230 240 250 260 270 280 290 2a0 2b0 2c0 2d0 2e0 2f0 300 310 320 330 340 350
  //   360 370 380 390 3a0 3b0 3c0 3d0 3e0 3f0 400 410 420 430 440 450 460 470 480 490 4a0 4b0 4c0 4d0 4e0
  //   4f0 500 510 520 530 540 550 560 570 580 590 5a0 5b0 5c0 5d0 5e0 5f0 600 610 620 630 640 650 660 670
  //   680 690 6a0 6b0 6c0 6d0 6e0 6f0 700 710 720 730 740 750 760 770 780 790 7a0 7b0 7c0 7d0 7e0 7f0 800
  //   810 820 830 840 850 860 870 880 890 8a0 8b0 8c0 8d0 8e0 8f0 900 910 920 930 940 950 960 970 980 990
  //   9a0 9b0 9c0 9d0 9e0 9f0 a00 a10 a20 a30 a40 a50 a60 a70 a80 a90 aa0 ab0 ac0 ad0 ae0 af0 b00 b10 b20
  //   b30 b40 b50 b60 b70 b80 b90 ba0 bb0 bc0 bd0 be0 bf0 c00 c10 c20 c30 c40 c50 c60 c70 c80 c90 ca0 cb0
  //   cc0 cd0 ce0 cf0 d00 d10 d20 d30 d40 d50 d60 d70 d80 d90 da0 db0 dc0 dd0 de0 df0 e00 e10 e20 e30 d40
  //   d50 d60 e70 e80 e90 ea0 eb0 ec0 ed0 ee0 ef0 f00 f10 f20 f30 f40 f50 f60 f70 f80 f90 fa0 fb0 fc0 fd0
  //   fe0 ff0
endmodule
