// Logisim project Proyectoparte2.circ as structural Verilog: 1 circuit, main circuit main
module main (
  input  in_1,
  input  in_2
);

  wire and_1_out, and_2_out, and_3_out, and_4_out, and_5_out, and_6_out, C0, C1, C2, CLK, nand_1_out,
       nor_1_out, not_1_out, or_1_out, or_2_out, or_3_out, or_4_out, or_5_out, S0, S0N, S1, S1N, S2, S2N;

  Clock clock_1 (.out(CLK));
  and and_1 (and_1_out, S2N, S1, S0);
  Counter #(.width(3), .max('h7)) counter_1 (
    .clr(1'b0), .load(in_2), .up(1'b0), .count(and_1_out), .clk(CLK), .D(3'b111), .Q({C2, C1, C0}));  // open: carry
  Hex_Digit_Display hex_digit_display_1 (.value(4'b0111));  // open: dp
  Hex_Digit_Display hex_digit_display_2 (.value({1'b0, C2, C1, C0}));  // open: dp
  or or_1 (or_1_out, S2, S1);
  or or_2 (or_2_out, S2, S0);
  nor nor_1 (nor_1_out, C0, C1, C2);
  not not_1 (not_1_out, in_1);
  and and_2 (and_2_out, or_1_out, or_2_out);
  and and_3 (and_3_out, S2N, S1N);
  or or_3 (or_3_out, in_1, S0);
  or or_4 (or_4_out, S1, S0, not_1_out);
  nand nand_1 (nand_1_out, S0, S1);
  or or_5 (or_5_out, S0, in_1);
  and and_4 (and_4_out, and_3_out, or_3_out);
  and and_5 (and_5_out, or_4_out, nand_1_out);
  D_Flip_Flop d_ff_1 (.D(and_6_out), .clk(CLK), .Q(S2), .Qn(S2N));  // open: preset, reset
  and and_6 (and_6_out, and_2_out, nor_1_out, or_5_out);
  D_Flip_Flop d_ff_2 (.D(and_4_out), .clk(CLK), .Q(S1), .Qn(S1N));  // open: preset, reset
  D_Flip_Flop d_ff_3 (.D(and_5_out), .clk(CLK), .Q(S0), .Qn(S0N));  // open: preset, reset

  // Other names for the same wires on the sheet: Q0 = in_1
endmodule
