// Logisim project Ejercicio3.circ as structural Verilog: 1 circuit, main circuit main
module main (
  input  M,
  input  B0,
  input  A0,
  input  A1,
  input  A2,
  input  A3,
  input  B1,
  input  B2,
  input  B3
);

  wire adder_1_cout, adder_1_out, adder_2_cout, adder_2_out, adder_3_cout, adder_3_out, adder_4_cout,
       adder_4_out, adder_5_cout, adder_5_out, adder_6_cout, adder_6_out, adder_7_cout, adder_7_out,
       adder_8_cout, adder_8_out, adder_9_cout, adder_9_out, multiplexer_1_out, multiplexer_2_out,
       multiplexer_3_out, multiplexer_4_out, or_1_out, xor_1_out, xor_2_out, xor_3_out, xor_4_out, xor_5_out,
       xor_6_out, xor_7_out, xor_8_out, xor_9_out, xor_10_out;

  xor xor_1 (xor_1_out, M, B0);
  xor xor_2 (xor_2_out, A0, A3);
  xor xor_3 (xor_3_out, xor_1_out, B3);
  xor xor_4 (xor_4_out, A0, A2);
  xor xor_5 (xor_5_out, xor_1_out, B2);
  xor xor_6 (xor_6_out, A0, A1);
  xor xor_7 (xor_7_out, xor_1_out, B1);
  Adder #(.width(1)) adder_1 (.a(xor_2_out), .b(xor_3_out), .out(adder_1_out), .cin(A0), .cout(adder_1_cout));
  Adder #(.width(1)) adder_2 (.a(xor_4_out), .b(xor_5_out), .out(adder_2_out), .cin(adder_1_cout), .cout(adder_2_cout));
  Adder #(.width(1)) adder_3 (.a(xor_6_out), .b(xor_7_out), .out(adder_3_out), .cin(adder_2_cout), .cout(adder_3_cout));
  Adder #(.width(1)) adder_4 (.a(adder_1_out), .b(1'b0), .out(adder_4_out), .cin(xor_1_out), .cout(adder_4_cout));
  Adder #(.width(1)) adder_5 (.a(adder_2_out), .b(1'b0), .out(adder_5_out), .cin(adder_4_cout), .cout(adder_5_cout));
  Adder #(.width(1)) adder_6 (.a(adder_3_out), .b(1'b0), .out(adder_6_out), .cin(adder_5_cout), .cout(adder_6_cout));
  or or_1 (or_1_out, xor_1_out, A0);
  xor xor_8 (xor_8_out, adder_6_out, adder_4_out);
  xor xor_9 (xor_9_out, adder_6_out, adder_5_out);
  xor xor_10 (xor_10_out, adder_6_out, adder_6_out);
  Adder #(.width(1)) adder_7 (.a(xor_8_out), .b(1'b0), .out(adder_7_out), .cin(adder_6_out), .cout(adder_7_cout));
  Adder #(.width(1)) adder_8 (.a(xor_9_out), .b(1'b0), .out(adder_8_out), .cin(adder_7_cout), .cout(adder_8_cout));
  Adder #(.width(1)) adder_9 (.a(xor_10_out), .b(1'b0), .out(adder_9_out), .cin(adder_8_cout), .cout(adder_9_cout));
  Multiplexer #(.enable("false")) multiplexer_1 (
    .in0(1'b0), .in1(adder_6_out), .out(multiplexer_1_out), .sel(or_1_out));
  Multiplexer #(.enable("false")) multiplexer_2 (
    .in0(adder_6_out), .in1(adder_9_out), .out(multiplexer_2_out), .sel(or_1_out));
  Multiplexer #(.enable("false")) multiplexer_3 (
    .in0(adder_5_out), .in1(adder_8_out), .out(multiplexer_3_out), .sel(or_1_out));
  Multiplexer #(.enable("false")) multiplexer_4 (
    .in0(adder_4_out), .in1(adder_7_out), .out(multiplexer_4_out), .sel(or_1_out));
  LED led_1 (.in(multiplexer_1_out));
  LED led_2 (.in(multiplexer_2_out));
  LED led_3 (.in(multiplexer_3_out));
  LED led_4 (.in(multiplexer_4_out));
endmodule
