// Logisim project Moore_FF_JK.circ as structural Verilog: 1 circuit, main circuit main
module main (
  input  Entrada
);

  wire and_1_out, and_2_out, clock_1_out, not_1_out, not_2_out, S0, S1;

  not not_1 (not_1_out, S1);
  not not_2 (not_2_out, Entrada);
  LED led_1 (.in(and_1_out));
  and and_1 (and_1_out, Entrada, not_1_out);
  LED led_2 (.in(and_2_out));
  and and_2 (and_2_out, Entrada, S0);
  LED led_3 (.in(not_2_out));
  J_K_Flip_Flop JK0 (.J(and_1_out), .K(1'b1), .clk(clock_1_out), .Q(S0));  // open: Qn, preset, reset
  J_K_Flip_Flop JK1 (.J(and_2_out), .K(not_2_out), .clk(clock_1_out), .Q(S1));  // open: Qn, preset, reset
  Clock clock_1 (.out(clock_1_out));
  LED led_4 (.in(S0));
  LED led_5 (.in(S1));
endmodule
