// Logisim project Moore_FF_T.circ as structural Verilog: 1 circuit, main circuit main
module main (
  input  Entrada
);

  wire and_1_out, and_2_out, and_3_out, clock_1_out, not_1_out, not_2_out, or_1_out, or_2_out, S0, S1;

  not not_1 (not_1_out, S1);
  not not_2 (not_2_out, Entrada);
  and and_1 (and_1_out, S0, Entrada);
  and and_2 (and_2_out, not_1_out, Entrada);
  and and_3 (and_3_out, not_2_out, S1);
  LED led_1 (.in(or_1_out));
  or or_1 (or_1_out, and_2_out, S0);
  LED led_2 (.in(or_2_out));
  or or_2 (or_2_out, and_1_out, and_3_out);
  T_Flip_Flop T0 (.T(or_1_out), .clk(clock_1_out), .Q(S0));  // open: Qn, reset, preset
  T_Flip_Flop T1 (.T(or_2_out), .clk(clock_1_out), .Q(S1));  // open: Qn, reset, preset
  Clock clock_1 (.out(clock_1_out));
endmodule
