// Logisim project Semaforo.circ as structural Verilog: 1 circuit, main circuit main
module main (
  input  Sns,
  input  Seo,
  input  rst
);

  wire and_1_out, and_2_out, and_3_out, and_4_out, and_5_out, and_6_out, and_7_out, and_8_out, and_9_out,
       clock_1_out, not_1_out, not_2_out, not_3_out, not_4_out, or_1_out, rgbled_1_p1, rgbled_1_p2,
       rgbled_2_p1, rgbled_2_p2, S0, S1, xor_3_out;

  not not_1 (not_1_out, S0);
  not not_2 (not_2_out, S1);
  not not_3 (not_3_out, Sns);
  not not_4 (not_4_out, Seo);
  and and_1 (and_1_out, not_2_out, not_3_out);
  and and_2 (and_2_out, S1, not_4_out);
  // RGBLED rgbled_1: pin names not known; wires that end beside it: rgbled_1_p1, rgbled_1_p2
  xor xor_1 (rgbled_1_p1, and_3_out, and_4_out);
  and and_3 (and_3_out, not_2_out, not_1_out);
  and and_4 (and_4_out, not_2_out, S0);
  and and_5 (and_5_out, S1, not_1_out);
  and and_6 (and_6_out, S1, S0);
  or or_1 (or_1_out, and_1_out, and_2_out);
  xor xor_2 (rgbled_1_p2, and_4_out, S1);
  LED led_1 (.in(and_3_out));
  LED led_2 (.in(and_4_out));
  LED led_3 (.in(S1));
  LED led_4 (.in(xor_3_out));
  xor xor_3 (xor_3_out, S1, S0);
  LED led_5 (.in(and_7_out));
  and and_7 (and_7_out, not_1_out, or_1_out);
  // RGBLED rgbled_2: pin names not known; wires that end beside it: rgbled_2_p1, rgbled_2_p2
  xor xor_4 (rgbled_2_p1, and_5_out, and_6_out);
  xor xor_5 (rgbled_2_p2, and_6_out, not_2_out);
  LED led_6 (.in(and_5_out));
  LED led_7 (.in(and_6_out));
  LED led_8 (.in(not_2_out));
  D_Flip_Flop u_S1 (.D(and_8_out), .clk(clock_1_out), .Q(S1));  // open: Qn, preset, reset
  and and_8 (and_8_out, xor_3_out, rst);
  and and_9 (and_9_out, and_7_out, rst);
  D_Flip_Flop u_S0 (.D(and_9_out), .clk(clock_1_out), .Q(S0));  // open: Qn, preset, reset
  Clock clock_1 (.out(clock_1_out));

  // Notes on the sheet:
  //   Lns
  //   Leo
endmodule
